// Logisim project 4x3memory_withRAM.circ as structural Verilog: 1 circuit, main circuit main
module main (
  input  [1:0] Chip_Select,
  input  [2:0] Input_Data,
  input  nCE,
  input  nWE,
  input  RESET,
  output [2:0] Output_Data
);

  wire Clock_out, not_1_out;

  Clock Clock (.out(Clock_out));
  RAM #(.addrWidth(2), .dataWidth(3), .bus("separate")) ram_1 (
    .addr(Chip_Select), .din(Input_Data), .data(Output_Data), .str(nWE), .sel(nCE), .clk(Clock_out),
    .ld(not_1_out), .clr(RESET));
  not not_1 (not_1_out, nWE);
endmodule
